// Logisim project stopwatch.circ as structural Verilog
module BCD_Counter (
  input  CLK,
  input  I0,
  input  I1,
  input  I2,
  input  I3,
  input  Load,
  input  Count,
  input  UP,
  input  CLR,
  output Q0,
  output Q1,
  output Q2,
  output Q3,
  output Trigger
);

  wire and_1_out, and_2_out, and_3_out, and_4_out, and_5_out, and_6_out, and_7_out, and_8_out, and_9_out,
       multiplexer_1_out, multiplexer_2_out, multiplexer_3_out, multiplexer_4_out, multiplexer_5_out,
       multiplexer_6_out, multiplexer_7_out, multiplexer_8_out, not_1_out, not_2_out, not_3_out, not_4_out,
       not_5_out, not_6_out, or_1_out, or_2_out, or_3_out, Q0_qn, Q1_qn, Q2_qn, Q3_qn;

  or or_1 (or_1_out, and_1_out, CLR);
  not not_1 (not_1_out, UP);
  and and_1 (and_1_out, UP, Q1, Q3, ~Load);  // AND_Gate
  and and_2 (and_2_out, not_3_out, ~Load, and_3_out);  // AND_Gate
  Multiplexer #(.select(3), .enable("false")) multiplexer_1 (
    .in0(1'b0), .in1(1'b0), .in2(not_1_out), .in3(UP), .in4(I0), .in5(I0), .in6(I0), .in7(I0),
    .out(multiplexer_1_out), .sel({Load, Count, UP}));
  not not_2 (not_2_out, multiplexer_1_out);
  not not_3 (not_3_out, UP);
  and and_3 (and_3_out, Q0, Q1, Q2, Q3);
  Multiplexer #(.enable("false")) multiplexer_2 (
    .in0(multiplexer_1_out), .in1(not_2_out), .out(multiplexer_2_out), .sel(Load));
  J_K_Flip_Flop #(.Pre_Clr_Positions("LEGACY")) u_Q0 (
    .J(multiplexer_1_out), .clk(CLK), .K(multiplexer_2_out), .Q(Q0), .Qn(Q0_qn), .preset(and_2_out),
    .reset(or_1_out));
  and and_4 (and_4_out, Q0_qn, not_1_out);
  and and_5 (and_5_out, Q0, UP);
  Multiplexer #(.select(3), .enable("false")) multiplexer_3 (
    .in0(1'b0), .in1(1'b0), .in2(and_4_out), .in3(and_5_out), .in4(I1), .in5(I1), .in6(I1), .in7(I1),
    .out(multiplexer_3_out), .sel({Load, Count, UP}));
  not not_4 (not_4_out, multiplexer_3_out);
  Multiplexer #(.enable("false")) multiplexer_4 (
    .in0(multiplexer_3_out), .in1(not_4_out), .out(multiplexer_4_out), .sel(Load));
  J_K_Flip_Flop #(.Pre_Clr_Positions("LEGACY")) u_Q1 (
    .J(multiplexer_3_out), .clk(CLK), .K(multiplexer_4_out), .Q(Q1), .Qn(Q1_qn), .reset(or_2_out));  // open: preset
  or or_2 (or_2_out, and_2_out, or_1_out);
  and and_6 (and_6_out, Q1, and_5_out);
  and and_7 (and_7_out, Q1_qn, and_4_out);
  Multiplexer #(.select(3), .enable("false")) multiplexer_5 (
    .in0(1'b0), .in1(1'b0), .in2(and_7_out), .in3(and_6_out), .in4(I2), .in5(I2), .in6(I2), .in7(I2),
    .out(multiplexer_5_out), .sel({Load, Count, UP}));
  not not_5 (not_5_out, multiplexer_5_out);
  Multiplexer #(.enable("false")) multiplexer_6 (
    .in0(multiplexer_5_out), .in1(not_5_out), .out(multiplexer_6_out), .sel(Load));
  J_K_Flip_Flop #(.Pre_Clr_Positions("LEGACY")) u_Q2 (
    .J(multiplexer_5_out), .clk(CLK), .K(multiplexer_6_out), .Q(Q2), .Qn(Q2_qn), .reset(or_3_out));  // open: preset
  or or_3 (or_3_out, and_2_out, or_1_out);
  and and_8 (and_8_out, Q2, and_6_out);
  and and_9 (and_9_out, Q2_qn, and_7_out);
  Multiplexer #(.select(3), .enable("false")) multiplexer_7 (
    .in0(1'b0), .in1(1'b0), .in2(and_9_out), .in3(and_8_out), .in4(I3), .in5(I3), .in6(I3), .in7(I3),
    .out(multiplexer_7_out), .sel({Load, Count, UP}));
  Multiplexer #(.enable("false")) multiplexer_8 (
    .in0(multiplexer_7_out), .in1(not_6_out), .out(multiplexer_8_out), .sel(Load));
  not not_6 (not_6_out, multiplexer_7_out);
  J_K_Flip_Flop #(.Pre_Clr_Positions("LEGACY")) u_Q3 (
    .J(multiplexer_7_out), .clk(CLK), .K(multiplexer_8_out), .Q(Q3), .Qn(Q3_qn), .preset(and_2_out),
    .reset(or_1_out));
  or or_4 (Trigger, or_1_out, and_2_out);
endmodule

module Seconds_To_Minutes (
  input  in_1,
  input  in_2,
  input  in_3,
  output out_4,
  output out_5,
  output out_6,
  output out_7
);

  BCD_Counter bcd_counter_1 ();  // open: CLK, I0, I1, I2, I3, Load, Count, UP, CLR, Q0, Q1, Q2, Q3, Trigger
  BCD_Counter S0 (
    .CLK(in_1), .Count(in_2), .UP(in_3), .Q0(out_4), .Q1(out_5), .Q2(out_6), .Q3(out_7));  // open: I0, I1, I2, I3, Load, CLR, Trigger
endmodule

module _1to6_Counter (
  input  CLK,
  input  I0,
  input  I1,
  input  I2,
  input  I3,
  input  Load,
  input  Count,
  input  UP,
  input  CLR,
  output Q0,
  output Q1,
  output Q2,
  output Q3,
  output Trigger
);

  wire and_1_out, and_2_out, and_3_out, and_4_out, and_5_out, and_6_out, and_7_out, and_8_out, and_9_out,
       multiplexer_1_out, multiplexer_2_out, multiplexer_3_out, multiplexer_4_out, multiplexer_5_out,
       multiplexer_6_out, multiplexer_7_out, multiplexer_8_out, not_1_out, not_2_out, not_3_out, not_4_out,
       not_5_out, not_6_out, or_1_out, or_2_out, or_3_out, Q0_qn, Q1_qn, Q2_qn, Q3_qn;

  or or_1 (or_1_out, and_1_out, CLR);
  not not_1 (not_1_out, UP);
  and and_1 (and_1_out, UP, Q1, Q2, ~Load);  // AND_Gate
  and and_2 (and_2_out, not_3_out, ~Load, and_3_out);  // AND_Gate
  Multiplexer #(.select(3), .enable("false")) multiplexer_1 (
    .in0(1'b0), .in1(1'b0), .in2(not_1_out), .in3(UP), .in4(I0), .in5(I0), .in6(I0), .in7(I0),
    .out(multiplexer_1_out), .sel({Load, Count, UP}));
  not not_2 (not_2_out, multiplexer_1_out);
  not not_3 (not_3_out, UP);
  and and_3 (and_3_out, Q0, Q1, Q2, Q3);
  Multiplexer #(.enable("false")) multiplexer_2 (
    .in0(multiplexer_1_out), .in1(not_2_out), .out(multiplexer_2_out), .sel(Load));
  J_K_Flip_Flop #(.Pre_Clr_Positions("LEGACY")) u_Q0 (
    .J(multiplexer_1_out), .clk(CLK), .K(multiplexer_2_out), .Q(Q0), .Qn(Q0_qn), .preset(and_2_out),
    .reset(or_1_out));
  and and_4 (and_4_out, Q0_qn, not_1_out);
  and and_5 (and_5_out, Q0, UP);
  Multiplexer #(.select(3), .enable("false")) multiplexer_3 (
    .in0(1'b0), .in1(1'b0), .in2(and_4_out), .in3(and_5_out), .in4(I1), .in5(I1), .in6(I1), .in7(I1),
    .out(multiplexer_3_out), .sel({Load, Count, UP}));
  not not_4 (not_4_out, multiplexer_3_out);
  Multiplexer #(.enable("false")) multiplexer_4 (
    .in0(multiplexer_3_out), .in1(not_4_out), .out(multiplexer_4_out), .sel(Load));
  J_K_Flip_Flop #(.Pre_Clr_Positions("LEGACY")) u_Q1 (
    .J(multiplexer_3_out), .clk(CLK), .K(multiplexer_4_out), .Q(Q1), .Qn(Q1_qn), .reset(or_2_out));  // open: preset
  or or_2 (or_2_out, and_2_out, or_1_out);
  and and_6 (and_6_out, Q1, and_5_out);
  and and_7 (and_7_out, Q1_qn, and_4_out);
  Multiplexer #(.select(3), .enable("false")) multiplexer_5 (
    .in0(1'b0), .in1(1'b0), .in2(and_7_out), .in3(and_6_out), .in4(I2), .in5(I2), .in6(I2), .in7(I2),
    .out(multiplexer_5_out), .sel({Load, Count, UP}));
  not not_5 (not_5_out, multiplexer_5_out);
  Multiplexer #(.enable("false")) multiplexer_6 (
    .in0(multiplexer_5_out), .in1(not_5_out), .out(multiplexer_6_out), .sel(Load));
  J_K_Flip_Flop #(.Pre_Clr_Positions("LEGACY")) u_Q2 (
    .J(multiplexer_5_out), .clk(CLK), .K(multiplexer_6_out), .Q(Q2), .Qn(Q2_qn), .preset(and_2_out),
    .reset(or_1_out));
  and and_8 (and_8_out, Q2, and_6_out);
  and and_9 (and_9_out, Q2_qn, and_7_out);
  Multiplexer #(.select(3), .enable("false")) multiplexer_7 (
    .in0(1'b0), .in1(1'b0), .in2(and_9_out), .in3(and_8_out), .in4(I3), .in5(I3), .in6(I3), .in7(I3),
    .out(multiplexer_7_out), .sel({Load, Count, UP}));
  Multiplexer #(.enable("false")) multiplexer_8 (
    .in0(multiplexer_7_out), .in1(not_6_out), .out(multiplexer_8_out), .sel(Load));
  not not_6 (not_6_out, multiplexer_7_out);
  or or_3 (or_3_out, and_2_out, or_1_out);
  J_K_Flip_Flop #(.Pre_Clr_Positions("LEGACY")) u_Q3 (
    .J(multiplexer_7_out), .clk(CLK), .K(multiplexer_8_out), .Q(Q3), .Qn(Q3_qn), .reset(or_3_out));  // open: preset
  or or_4 (Trigger, or_1_out, and_2_out);
endmodule

module BCD_Counter_Modified (
  input  CLK,
  input  I1,
  input  I0,
  input  I2,
  input  I3,
  input  Load,
  input  Count,
  input  UP,
  input  CLR,
  output Q0,
  output Q1,
  output Q2,
  output Q3,
  output Trigger
);

  wire and_1_out, and_2_out, and_3_out, and_4_out, and_5_out, and_6_out, and_7_out, and_8_out, and_9_out,
       multiplexer_1_out, multiplexer_2_out, multiplexer_3_out, multiplexer_4_out, multiplexer_5_out,
       multiplexer_6_out, multiplexer_7_out, multiplexer_8_out, not_1_out, not_2_out, not_3_out, not_4_out,
       not_5_out, or_1_out, or_2_out, or_3_out, Q0_qn, Q1_qn, Q2_qn, Q3_qn;

  or or_1 (or_1_out, and_1_out, CLR);
  not not_1 (not_1_out, UP);
  and and_1 (and_1_out, ~Q0, UP, Q1, ~Q3, Load, ~Q2);  // AND_Gate
  Multiplexer #(.select(3), .enable("false")) multiplexer_1 (
    .in0(1'b0), .in1(1'b0), .in2(not_1_out), .in3(UP), .in4(I0), .in5(I0), .in6(I0), .in7(I0),
    .out(multiplexer_1_out), .sel({Load, Count, UP}));
  not not_2 (not_2_out, multiplexer_1_out);
  and and_2 (and_2_out, ~CLK, ~Q0, ~Q1, ~Q2, ~Q3, not_1_out);  // AND_Gate
  and and_3 (and_3_out, ~Q0, ~Q1, ~Q2, ~Q3, ~CLK, ~or_1_out, UP);  // AND_Gate
  Multiplexer #(.enable("false")) multiplexer_2 (
    .in0(multiplexer_1_out), .in1(not_2_out), .out(multiplexer_2_out), .sel(Load));
  J_K_Flip_Flop #(.Pre_Clr_Positions("LEGACY")) u_Q0 (
    .J(multiplexer_1_out), .clk(CLK), .K(multiplexer_2_out), .Q(Q0), .Qn(Q0_qn), .preset(and_2_out),
    .reset(or_1_out));
  and and_4 (and_4_out, Q0_qn, not_1_out);
  and and_5 (and_5_out, Q0, UP);
  Multiplexer #(.select(3), .enable("false")) multiplexer_3 (
    .in0(1'b0), .in1(1'b0), .in2(and_4_out), .in3(and_5_out), .in4(I1), .in5(I1), .in6(I1), .in7(I1),
    .out(multiplexer_3_out), .sel({Load, Count, UP}));
  not not_3 (not_3_out, multiplexer_3_out);
  Multiplexer #(.enable("false")) multiplexer_4 (
    .in0(multiplexer_3_out), .in1(not_3_out), .out(multiplexer_4_out), .sel(Load));
  J_K_Flip_Flop #(.Pre_Clr_Positions("LEGACY")) u_Q1 (
    .J(multiplexer_3_out), .clk(CLK), .K(multiplexer_4_out), .Q(Q1), .Qn(Q1_qn), .reset(or_2_out));  // open: preset
  or or_2 (or_2_out, and_2_out, or_1_out);
  and and_6 (and_6_out, Q1, and_5_out);
  and and_7 (and_7_out, Q1_qn, and_4_out);
  Multiplexer #(.select(3), .enable("false")) multiplexer_5 (
    .in0(1'b0), .in1(1'b0), .in2(and_7_out), .in3(and_6_out), .in4(I2), .in5(I2), .in6(I2), .in7(I2),
    .out(multiplexer_5_out), .sel({Load, Count, UP}));
  not not_4 (not_4_out, multiplexer_5_out);
  Multiplexer #(.enable("false")) multiplexer_6 (
    .in0(multiplexer_5_out), .in1(not_4_out), .out(multiplexer_6_out), .sel(Load));
  J_K_Flip_Flop #(.Pre_Clr_Positions("LEGACY")) u_Q2 (
    .J(multiplexer_5_out), .clk(CLK), .K(multiplexer_6_out), .Q(Q2), .Qn(Q2_qn), .reset(or_3_out));  // open: preset
  or or_3 (or_3_out, and_2_out, or_1_out);
  and and_8 (and_8_out, Q2, and_6_out);
  and and_9 (and_9_out, Q2_qn, and_7_out);
  Multiplexer #(.select(3), .enable("false")) multiplexer_7 (
    .in0(1'b0), .in1(1'b0), .in2(and_9_out), .in3(and_8_out), .in4(I3), .in5(I3), .in6(I3), .in7(I3),
    .out(multiplexer_7_out), .sel({Load, Count, UP}));
  Multiplexer #(.enable("false")) multiplexer_8 (
    .in0(multiplexer_7_out), .in1(not_5_out), .out(multiplexer_8_out), .sel(Load));
  not not_5 (not_5_out, multiplexer_7_out);
  J_K_Flip_Flop #(.Pre_Clr_Positions("LEGACY")) u_Q3 (
    .J(multiplexer_7_out), .clk(CLK), .K(multiplexer_8_out), .Q(Q3), .Qn(Q3_qn), .preset(and_2_out),
    .reset(or_1_out));
  or or_4 (Trigger, and_2_out, and_3_out);
endmodule
